// Digital circuit Sap-1.dig as structural Verilog
module Sap_1 (
  input  Cp,
  input  Clk,
  input  Clr,
  input  Ep,
  input  La,
  input  Ea,
  input  Clk_2,
  input  Su,
  input  Eu,
  input  Lb,
  input  Clk_3,
  input  [1:0] Lm,
  input  Clk_4,
  input  Clk_5,
  input  CE,
  input  Li,
  input  Clk_6,
  input  Ei,
  input  Clr_2,
  input  Clk_7,
  input  Lo,
  input  Clr_3,
  output out_23,
  output out_24,
  output out_25,
  output out_26,
  output out_27,
  output out_28,
  output out_29,
  output out_30
);

  wire Contador_de_programas_out, not_1_out, not_2_out, reg_8b_q;
  wire [1:0] undriven;

  not not_1 (not_1_out, CE);
  LookUpTable Contador_de_programas (.in0(Cp), .in1(Clk), .in2(Clr), .in3(Ep), .out(Contador_de_programas_out));
  ROM rom_1 (.A(Lm), .sel(Clk_4), .D(Contador_de_programas_out));
  BlockRAMDualPort blockramdualport_1 (
    .A(undriven), .Din(not_1_out), .str(not_1_out), .C(Clk_5), .D(Contador_de_programas_out));
  LookUpTable \Registrador_de_instrução  (
    .in0(Li), .in1(Clk_6), .in2(Ei), .in3(Clr_2), .out(Contador_de_programas_out));
  not not_2 (not_2_out, Lo);
  Register reg_8b (.D(Contador_de_programas_out), .C(Clk_7), .en(Clr_3), .Q(reg_8b_q));
  Add add_1 (.a(Ea), .b(Clk_2), .c_i(La), .s(Contador_de_programas_out), .c_o(Contador_de_programas_out));
  LookUpTable Somador_Subtrator (.in0(Eu), .in1(Su), .out(Contador_de_programas_out));
  LookUpTable Registrador_B (.in0(Clk_3), .in1(Lb), .out(Contador_de_programas_out));
  Switch switch_1 (.A(reg_8b_q), .B(out_23));
  // Pins of 1 and 2 bits meet at Lm

  assign out_24 = out_23;
  assign out_25 = out_23;
  assign out_26 = out_23;
  assign out_27 = out_23;
  assign out_28 = out_23;
  assign out_29 = out_23;
  assign out_30 = out_23;
endmodule
